// Logisim project testes_adders.circ as structural Verilog: 2 circuits, main circuit main
module FA (
  input  A,
  input  B,
  input  Cin,
  output Cout,
  output S
);

  wire and_1_out, and_2_out, or_2_out, xor_1_out;

  or or_1 (Cout, and_1_out, and_2_out);
  and and_1 (and_1_out, A, B);
  and and_2 (and_2_out, Cin, or_2_out);
  or or_2 (or_2_out, A, B);
  xor xor_1 (xor_1_out, A, B);
  xor xor_2 (S, xor_1_out, Cin);
endmodule

module main (
  input  in_1,
  input  in_2,
  input  A,
  input  B,
  output out_5,
  output out_6,
  output out_7,
  output out_8,
  output out_9,
  output out_10,
  output out_11,
  output out_12,
  output out_13,
  output out_14,
  output out_15,
  output out_16,
  output out_17,
  output out_18,
  output out_19,
  output out_20,
  output out_21,
  output out_22,
  output out_23,
  output out_24,
  output out_25,
  output out_26,
  output out_27,
  output out_28,
  output out_29,
  output out_30,
  output out_31,
  output out_32,
  output out_33,
  output out_34,
  output out_35,
  output out_36,
  output out_37,
  output out_38,
  output out_39,
  output out_40,
  output out_41,
  output out_42,
  output out_43,
  output out_44,
  output out_45,
  output out_46,
  output out_47,
  output out_48,
  output out_49,
  output out_50,
  output out_51,
  output out_52,
  output out_53,
  output out_54,
  output out_55,
  output out_56,
  output out_57,
  output out_58,
  output out_59,
  output out_60,
  output out_61,
  output out_62,
  output out_63,
  output out_64,
  output out_65,
  output out_66,
  output out_67,
  output out_68,
  output out_69,
  output out_70
);

  wire fa_2_cout, fa_2_s, fa_3_cout, fa_4_cout, fa_4_s, fa_5_cout, fa_5_s, fa_6_cout, fa_7_cout, fa_7_s,
       fa_8_cout, fa_9_cout, fa_9_s, fa_10_cout, fa_10_s, fa_11_cout, fa_12_cout, fa_12_s, fa_13_cout,
       fa_13_s, fa_14_cout, fa_15_cout, fa_16_cout, fa_16_s, fa_17_cout, fa_17_s, fa_18_cout, fa_19_cout,
       fa_20_cout, fa_20_s, fa_21_cout, fa_21_s, fa_22_cout, fa_23_cout, fa_23_s, fa_24_cout, fa_24_s,
       fa_25_cout, fa_26_cout, fa_26_s, fa_27_cout, fa_28_cout, fa_28_s, fa_29_cout, fa_30_cout, fa_30_s,
       fa_31_cout, fa_31_s, fa_32_cout, fa_33_cout, fa_33_s, fa_34_cout, fa_35_cout, fa_35_s, fa_36_cout,
       fa_36_s, fa_37_cout, fa_38_cout, fa_39_cout, fa_39_s, fa_40_cout, fa_40_s, fa_41_cout, fa_42_cout,
       fa_42_s, fa_43_cout, fa_44_cout, fa_44_s, fa_45_cout, fa_46_cout, fa_46_s, fa_47_cout, fa_47_s,
       fa_48_cout, fa_49_cout, fa_49_s, fa_50_cout, fa_50_s, fa_51_cout, fa_52_cout, fa_52_s, fa_53_cout,
       fa_53_s, fa_54_cout, fa_55_cout, fa_55_s, fa_56_cout, fa_57_cout, fa_58_cout, fa_58_s, fa_59_cout,
       fa_60_cout, fa_60_s, fa_61_cout, fa_61_s, fa_62_cout, fa_63_cout, fa_63_s, fa_64_cout, fa_65_cout,
       fa_65_s, fa_66_cout, fa_66_s, fa_67_cout, fa_68_cout, fa_68_s, fa_69_cout, fa_69_s, fa_70_cout,
       fa_71_cout, fa_72_cout, fa_72_s, fa_73_cout, fa_73_s, fa_74_cout, fa_75_cout, fa_75_s, fa_76_cout,
       fa_76_s, fa_77_cout, fa_77_s, fa_78_cout, fa_78_s, fa_79_cout, fa_79_s, fa_80_cout, fa_80_s,
       fa_81_cout, fa_81_s, fa_82_cout, fa_82_s, fa_83_cout, fa_83_s, fa_84_cout, fa_84_s, fa_85_cout,
       fa_85_s, fa_86_cout, fa_86_s, fa_87_cout, fa_87_s, fa_88_cout, fa_88_s, fa_89_cout, fa_90_cout,
       fa_91_cout, fa_92_cout, multiplexer_6_out, multiplexer_11_out, multiplexer_15_out, multiplexer_20_out,
       multiplexer_26_out, multiplexer_31_out;

  FA fa_1 (.A(A), .B(B), .Cin(fa_3_cout), .Cout(out_5), .S(out_6));
  FA fa_2 (.A(A), .B(B), .Cin(fa_5_cout), .Cout(fa_2_cout), .S(fa_2_s));
  Multiplexer multiplexer_1 (.in0(fa_2_cout), .in1(fa_4_cout), .out(out_38), .sel(multiplexer_6_out));
  FA fa_3 (.A(A), .B(B), .Cin(fa_6_cout), .Cout(fa_3_cout), .S(out_7));
  FA fa_4 (.A(A), .B(B), .Cin(fa_7_cout), .Cout(fa_4_cout), .S(fa_4_s));
  FA fa_5 (.A(A), .B(B), .Cin(fa_10_cout), .Cout(fa_5_cout), .S(fa_5_s));
  Multiplexer multiplexer_2 (.in0(fa_2_s), .in1(fa_4_s), .out(out_39));  // open: sel
  FA fa_6 (.A(A), .B(B), .Cin(fa_8_cout), .Cout(fa_6_cout), .S(out_8));
  FA fa_7 (.A(A), .B(B), .Cin(fa_9_cout), .Cout(fa_7_cout), .S(fa_7_s));
  Multiplexer multiplexer_3 (.in0(fa_5_s), .in1(fa_7_s), .out(out_40));  // open: sel
  FA fa_8 (.A(A), .B(B), .Cin(fa_11_cout), .Cout(fa_8_cout), .S(out_9));
  FA fa_9 (.A(A), .B(B), .Cin(fa_12_cout), .Cout(fa_9_cout), .S(fa_9_s));
  FA fa_10 (.A(A), .B(B), .Cin(fa_13_cout), .Cout(fa_10_cout), .S(fa_10_s));
  Multiplexer multiplexer_4 (.in0(fa_10_s), .in1(fa_9_s), .out(out_41));  // open: sel
  FA fa_11 (.A(A), .B(B), .Cin(fa_14_cout), .Cout(fa_11_cout), .S(out_10));
  FA fa_12 (.A(A), .B(B), .Cin(1'b1), .Cout(fa_12_cout), .S(fa_12_s));
  FA fa_13 (.A(A), .B(B), .Cin(1'b0), .Cout(fa_13_cout), .S(fa_13_s));
  Multiplexer multiplexer_5 (.in0(fa_13_s), .in1(fa_12_s), .out(out_42));  // open: sel
  FA fa_14 (.A(A), .B(B), .Cin(fa_15_cout), .Cout(fa_14_cout), .S(out_11));
  Multiplexer multiplexer_6 (.in0(fa_17_cout), .in1(fa_16_cout), .out(multiplexer_6_out), .sel(multiplexer_11_out));
  FA fa_15 (.A(A), .B(B), .Cin(fa_18_cout), .Cout(fa_15_cout), .S(out_12));
  FA fa_16 (.A(A), .B(B), .Cin(fa_20_cout), .Cout(fa_16_cout), .S(fa_16_s));
  FA fa_17 (.A(A), .B(B), .Cin(fa_21_cout), .Cout(fa_17_cout), .S(fa_17_s));
  Multiplexer multiplexer_7 (.in0(fa_17_s), .in1(fa_16_s), .out(out_43));  // open: sel
  FA fa_18 (.A(A), .B(B), .Cin(fa_19_cout), .Cout(fa_18_cout), .S(out_13));
  FA fa_19 (.A(A), .B(B), .Cin(fa_22_cout), .Cout(fa_19_cout), .S(out_14));
  FA fa_20 (.A(A), .B(B), .Cin(fa_23_cout), .Cout(fa_20_cout), .S(fa_20_s));
  FA fa_21 (.A(A), .B(B), .Cin(fa_24_cout), .Cout(fa_21_cout), .S(fa_21_s));
  Multiplexer multiplexer_8 (.in0(fa_21_s), .in1(fa_20_s), .out(out_44));  // open: sel
  FA fa_22 (.A(A), .B(B), .Cin(fa_25_cout), .Cout(fa_22_cout), .S(out_15));
  FA fa_23 (.A(A), .B(B), .Cin(fa_28_cout), .Cout(fa_23_cout), .S(fa_23_s));
  FA fa_24 (.A(A), .B(B), .Cin(fa_26_cout), .Cout(fa_24_cout), .S(fa_24_s));
  Multiplexer multiplexer_9 (.in0(fa_24_s), .in1(fa_23_s), .out(out_45));  // open: sel
  FA fa_25 (.A(A), .B(B), .Cin(fa_27_cout), .Cout(fa_25_cout), .S(out_16));
  FA fa_26 (.A(A), .B(B), .Cin(1'b0), .Cout(fa_26_cout), .S(fa_26_s));
  Multiplexer multiplexer_10 (.in0(fa_26_s), .in1(fa_28_s), .out(out_46));  // open: sel
  FA fa_27 (.A(A), .B(B), .Cin(fa_29_cout), .Cout(fa_27_cout), .S(out_17));
  FA fa_28 (.A(A), .B(B), .Cin(1'b1), .Cout(fa_28_cout), .S(fa_28_s));
  Multiplexer multiplexer_11 (.in0(fa_31_cout), .in1(fa_30_cout), .out(multiplexer_11_out), .sel(multiplexer_15_out));
  FA fa_29 (.A(A), .B(B), .Cin(fa_32_cout), .Cout(fa_29_cout), .S(out_18));
  FA fa_30 (.A(A), .B(B), .Cin(fa_35_cout), .Cout(fa_30_cout), .S(fa_30_s));
  FA fa_31 (.A(A), .B(B), .Cin(fa_33_cout), .Cout(fa_31_cout), .S(fa_31_s));
  Multiplexer multiplexer_12 (.in0(fa_31_s), .in1(fa_30_s), .out(out_47));  // open: sel
  FA fa_32 (.A(A), .B(B), .Cin(fa_34_cout), .Cout(fa_32_cout), .S(out_19));
  FA fa_33 (.A(A), .B(B), .Cin(fa_36_cout), .Cout(fa_33_cout), .S(fa_33_s));
  Multiplexer multiplexer_13 (.in0(fa_33_s), .in1(fa_35_s), .out(out_48));  // open: sel
  FA fa_34 (.A(A), .B(B), .Cin(fa_37_cout), .Cout(fa_34_cout), .S(out_20));
  FA fa_35 (.A(A), .B(B), .Cin(fa_39_cout), .Cout(fa_35_cout), .S(fa_35_s));
  FA fa_36 (.A(A), .B(B), .Cin(fa_40_cout), .Cout(fa_36_cout), .S(fa_36_s));
  FA fa_37 (.A(A), .B(B), .Cin(fa_38_cout), .Cout(fa_37_cout), .S(out_21));
  FA fa_38 (.A(A), .B(B), .Cin(fa_41_cout), .Cout(fa_38_cout), .S(out_22));
  FA fa_39 (.A(A), .B(B), .Cin(fa_42_cout), .Cout(fa_39_cout), .S(fa_39_s));
  FA fa_40 (.A(A), .B(B), .Cin(1'b0), .Cout(fa_40_cout), .S(fa_40_s));
  Multiplexer multiplexer_14 (.in0(fa_36_s), .in1(fa_39_s), .out(out_49));  // open: sel
  FA fa_41 (.A(A), .B(B), .Cin(fa_43_cout), .Cout(fa_41_cout), .S(out_23));
  FA fa_42 (.A(A), .B(B), .Cin(1'b1), .Cout(fa_42_cout), .S(fa_42_s));
  Multiplexer multiplexer_15 (.in0(fa_44_cout), .in1(fa_46_cout), .out(multiplexer_15_out), .sel(multiplexer_20_out));
  Multiplexer multiplexer_16 (.in0(fa_40_s), .in1(fa_42_s), .out(out_50));  // open: sel
  FA fa_43 (.A(A), .B(B), .Cin(fa_45_cout), .Cout(fa_43_cout), .S(out_24));
  FA fa_44 (.A(A), .B(B), .Cin(fa_47_cout), .Cout(fa_44_cout), .S(fa_44_s));
  FA fa_45 (.A(A), .B(B), .Cin(fa_48_cout), .Cout(fa_45_cout), .S(out_25));
  FA fa_46 (.A(A), .B(B), .Cin(fa_49_cout), .Cout(fa_46_cout), .S(fa_46_s));
  FA fa_47 (.A(A), .B(B), .Cin(fa_50_cout), .Cout(fa_47_cout), .S(fa_47_s));
  Multiplexer multiplexer_17 (.in0(fa_44_s), .in1(fa_46_s), .out(out_51));  // open: sel
  FA fa_48 (.A(A), .B(B), .Cin(fa_51_cout), .Cout(fa_48_cout), .S(out_26));
  FA fa_49 (.A(A), .B(B), .Cin(fa_52_cout), .Cout(fa_49_cout), .S(fa_49_s));
  FA fa_50 (.A(A), .B(B), .Cin(fa_53_cout), .Cout(fa_50_cout), .S(fa_50_s));
  Multiplexer multiplexer_18 (.in0(fa_47_s), .in1(fa_49_s), .out(out_52));  // open: sel
  FA fa_51 (.A(A), .B(B), .Cin(fa_54_cout), .Cout(fa_51_cout), .S(out_27));
  FA fa_52 (.A(A), .B(B), .Cin(fa_55_cout), .Cout(fa_52_cout), .S(fa_52_s));
  FA fa_53 (.A(A), .B(B), .Cin(1'b0), .Cout(fa_53_cout), .S(fa_53_s));
  Multiplexer multiplexer_19 (.in0(fa_50_s), .in1(fa_52_s), .out(out_53));  // open: sel
  FA fa_54 (.A(A), .B(B), .Cin(fa_56_cout), .Cout(fa_54_cout), .S(out_28));
  FA fa_55 (.A(A), .B(B), .Cin(1'b1), .Cout(fa_55_cout), .S(fa_55_s));
  Multiplexer multiplexer_20 (.in0(fa_58_cout), .in1(fa_60_cout), .out(multiplexer_20_out), .sel(multiplexer_26_out));
  Multiplexer multiplexer_21 (.in0(fa_53_s), .in1(fa_55_s), .out(out_54));  // open: sel
  FA fa_56 (.A(A), .B(B), .Cin(fa_57_cout), .Cout(fa_56_cout), .S(out_29));
  FA fa_57 (.A(A), .B(B), .Cin(fa_59_cout), .Cout(fa_57_cout), .S(out_30));
  FA fa_58 (.A(A), .B(B), .Cin(fa_61_cout), .Cout(fa_58_cout), .S(fa_58_s));
  FA fa_59 (.A(A), .B(B), .Cin(fa_62_cout), .Cout(fa_59_cout), .S(out_31));
  FA fa_60 (.A(A), .B(B), .Cin(fa_63_cout), .Cout(fa_60_cout), .S(fa_60_s));
  FA fa_61 (.A(A), .B(B), .Cin(fa_66_cout), .Cout(fa_61_cout), .S(fa_61_s));
  Multiplexer multiplexer_22 (.in0(fa_58_s), .in1(fa_60_s), .out(out_55));  // open: sel
  FA fa_62 (.A(A), .B(B), .Cin(fa_64_cout), .Cout(fa_62_cout), .S(out_32));
  FA fa_63 (.A(A), .B(B), .Cin(fa_65_cout), .Cout(fa_63_cout), .S(fa_63_s));
  Multiplexer multiplexer_23 (.in0(fa_61_s), .in1(fa_63_s), .out(out_56));  // open: sel
  FA fa_64 (.A(A), .B(B), .Cin(fa_67_cout), .Cout(fa_64_cout), .S(out_33));
  FA fa_65 (.A(A), .B(B), .Cin(fa_68_cout), .Cout(fa_65_cout), .S(fa_65_s));
  FA fa_66 (.A(A), .B(B), .Cin(fa_69_cout), .Cout(fa_66_cout), .S(fa_66_s));
  Multiplexer multiplexer_24 (.in0(fa_66_s), .in1(fa_65_s), .out(out_57));  // open: sel
  FA fa_67 (.A(A), .B(B), .Cin(fa_70_cout), .Cout(fa_67_cout), .S(out_34));
  FA fa_68 (.A(A), .B(B), .Cin(1'b1), .Cout(fa_68_cout), .S(fa_68_s));
  FA fa_69 (.A(A), .B(B), .Cin(1'b0), .Cout(fa_69_cout), .S(fa_69_s));
  Multiplexer multiplexer_25 (.in0(fa_69_s), .in1(fa_68_s), .out(out_58));  // open: sel
  FA fa_70 (.A(A), .B(B), .Cin(fa_71_cout), .Cout(fa_70_cout), .S(out_35));
  Multiplexer multiplexer_26 (.in0(fa_73_cout), .in1(fa_72_cout), .out(multiplexer_26_out), .sel(multiplexer_31_out));
  FA fa_71 (.A(A), .B(B), .Cin(fa_74_cout), .Cout(fa_71_cout), .S(out_36));
  FA fa_72 (.A(A), .B(B), .Cin(fa_75_cout), .Cout(fa_72_cout), .S(fa_72_s));
  FA fa_73 (.A(A), .B(B), .Cin(fa_76_cout), .Cout(fa_73_cout), .S(fa_73_s));
  Multiplexer multiplexer_27 (.in0(fa_73_s), .in1(fa_72_s), .out(out_59));  // open: sel
  FA fa_74 (.A(A), .B(B), .Cin(in_1), .Cout(fa_74_cout), .S(out_37));
  FA fa_75 (.A(A), .B(B), .Cin(fa_77_cout), .Cout(fa_75_cout), .S(fa_75_s));
  FA fa_76 (.A(A), .B(B), .Cin(fa_78_cout), .Cout(fa_76_cout), .S(fa_76_s));
  Multiplexer multiplexer_28 (.in0(fa_76_s), .in1(fa_75_s), .out(out_60));  // open: sel
  FA fa_77 (.A(A), .B(B), .Cin(fa_80_cout), .Cout(fa_77_cout), .S(fa_77_s));
  FA fa_78 (.A(A), .B(B), .Cin(fa_79_cout), .Cout(fa_78_cout), .S(fa_78_s));
  Multiplexer multiplexer_29 (.in0(fa_78_s), .in1(fa_77_s), .out(out_61));  // open: sel
  FA fa_79 (.A(A), .B(B), .Cin(1'b0), .Cout(fa_79_cout), .S(fa_79_s));
  Multiplexer multiplexer_30 (.in0(fa_79_s), .in1(fa_80_s), .out(out_62));  // open: sel
  FA fa_80 (.A(A), .B(B), .Cin(1'b1), .Cout(fa_80_cout), .S(fa_80_s));
  Multiplexer multiplexer_31 (.in0(fa_82_cout), .in1(fa_81_cout), .out(multiplexer_31_out), .sel(fa_89_cout));
  FA fa_81 (.A(A), .B(B), .Cin(fa_84_cout), .Cout(fa_81_cout), .S(fa_81_s));
  FA fa_82 (.A(A), .B(B), .Cin(fa_83_cout), .Cout(fa_82_cout), .S(fa_82_s));
  Multiplexer multiplexer_32 (.in0(fa_82_s), .in1(fa_81_s), .out(out_63));  // open: sel
  FA fa_83 (.A(A), .B(B), .Cin(fa_85_cout), .Cout(fa_83_cout), .S(fa_83_s));
  Multiplexer multiplexer_33 (.in0(fa_83_s), .in1(fa_84_s), .out(out_64));  // open: sel
  FA fa_84 (.A(A), .B(B), .Cin(fa_86_cout), .Cout(fa_84_cout), .S(fa_84_s));
  FA fa_85 (.A(A), .B(B), .Cin(fa_87_cout), .Cout(fa_85_cout), .S(fa_85_s));
  FA fa_86 (.A(A), .B(B), .Cin(fa_88_cout), .Cout(fa_86_cout), .S(fa_86_s));
  FA fa_87 (.A(A), .B(B), .Cin(1'b0), .Cout(fa_87_cout), .S(fa_87_s));
  Multiplexer multiplexer_34 (.in0(fa_85_s), .in1(fa_86_s), .out(out_65));  // open: sel
  FA fa_88 (.A(A), .B(B), .Cin(1'b1), .Cout(fa_88_cout), .S(fa_88_s));
  Multiplexer multiplexer_35 (.in0(fa_87_s), .in1(fa_88_s), .out(out_66));  // open: sel
  FA fa_89 (.A(A), .B(B), .Cin(fa_90_cout), .Cout(fa_89_cout), .S(out_67));
  FA fa_90 (.A(A), .B(B), .Cin(fa_91_cout), .Cout(fa_90_cout), .S(out_68));
  FA fa_91 (.A(A), .B(B), .Cin(fa_92_cout), .Cout(fa_91_cout), .S(out_69));
  FA fa_92 (.A(A), .B(B), .Cin(in_2), .Cout(fa_92_cout), .S(out_70));
endmodule
